# Fritzing sketch jueves2 (saved by Fritzing 0.9.1b)
breadboards: 1

parts:
  LED1 = RGB LED (com. cathode, rgb) [package="5 mm [THT]"]
  Part1 = Arduino Uno (Rev3)
  R1 = Resistor [tolerance=±5% resistance=470 package=THT]
  R2 = Resistor [tolerance=±5% resistance=470 package=THT]
  R3 = Resistor [tolerance=±5% resistance=470 package=THT]

nets:
  N1: LED1.red_anode, R1.Pin_0
  GND: LED1.common_cathode
  N2: LED1.green_anode, R3.Pin_0
  N3: LED1.blue_anode, R2.Pin_0
  N4: Part1.D9_PWM, R1.Pin_1
  N5: Part1.D10_PWM/SS, R2.Pin_1
  N6: Part1.D11_PWM/MOSI, R3.Pin_1
