# Fritzing sketch jueves3 (saved by Fritzing 0.9.1b)
breadboards: 1

parts:
  J1 = Basic Servo
  Part1 = Arduino Uno (Rev3)
  R1 = Rotary Potentiometer (Small) [maximum_resistance=100kΩ package=THT]

nets:
  GND: J1.gnd, Part1.GND, R1.leg1
  VCC: J1.vcc, Part1.5V, R1.leg2
  N1: J1.pulse, Part1.D9_PWM
  N2: Part1.A0, R1.wiper
