# Fritzing sketch jueves4 (saved by Fritzing 0.9.1b)

parts:
  R1 = Photocell (LDR) [package=THT]
  Part1 = Arduino Uno (Rev3)
  J1 = Piezo Speaker
  R2 = Resistor [tolerance=±5% resistance=470 package=THT]
  R3 = Resistor [tolerance=±5% resistance=470 package=THT]

nets:
  N1: R1.pin_0, Part1.A0, R2.Pin_1
  N2: R1.pin_1, Part1.GND, J1.pin2
  N3: Part1.D8, R3.Pin_0
  N4: Part1.5V, R2.Pin_0
  N5: J1.pin1, R3.Pin_1
