# Fritzing sketch martes2 (saved by Fritzing 0.9.1b)
breadboards: 1

parts:
  Part1 = Arduino Uno (Rev3)
  S1 = Pushbutton [package="[THT]"]
  R1 = Resistor [tolerance=±5% resistance=10k package=THT]

nets:
  N1: Part1.D12/MISO, S1.Pin_4, R1.Pin_1
  N2: Part1.GND, S1.Pin_2
  N3: Part1.5V, R1.Pin_0
