# Fritzing sketch martes_led_botao (saved by Fritzing 0.9.1b)
breadboards: 1

parts:
  R1 = Resistor [tolerance=±5% resistance=470 package=THT]
  LED1 = LED - 5mm [color="Red (633nm)" package="5 mm [THT]"]
  S2 = Pushbutton [package=THT]

nets:
  5V: R1.Pin_0
  N1: R1.Pin_1, LED1.anode
  N2: LED1.cathode, S2.leg0
  GND: S2.leg1
