# Fritzing sketch martes_leds (saved by Fritzing 0.9.1b)
breadboards: 1

parts:
  Componente1 = Arduino Uno (Rev3)
  R1 = Resistor [tolerance=±5% resistance=470 package=THT]
  LED1 = LED - 5mm [color="Red (633nm)" package="5 mm [THT]"]
  LED2 = LED - 5mm [color="Green (555nm)" package="5 mm [THT]"]
  R2 = Resistor [tolerance=±5% resistance=470 package=THT]

nets:
  N1: Componente1.5V, LED1.anode, LED2.anode
  N2: Componente1.GND, R1.Pin_0, R2.Pin_0
  N3: R1.Pin_1, LED1.cathode
  N4: LED2.cathode, R2.Pin_1
