# Fritzing sketch miercoles1_3 (saved by Fritzing 0.9.1b)
breadboards: 1

parts:
  Q1 = LTR-301 [package=ltr-301]
  LED1 = LED - 5mm [color="Red (633nm)" package="5 mm [THT]"]
  R1 = Resistor [tolerance=±5% resistance=220 package=THT]
  R2 = Resistor [tolerance=±5% resistance=220 package=THT]

nets:
  Vout: Q1.C, R2.Pin_1
  GND: Q1.E, LED1.cathode
  N1: LED1.anode, R1.Pin_1
  5V: R1.Pin_0, R2.Pin_0
