# Fritzing sketch miercoles2 (saved by Fritzing 0.9.1b)
breadboards: 1

parts:
  Part1 = Arduino Uno (Rev3)
  LED1 = LED - 5mm [color="Red (633nm)" package="5 mm [THT]"]
  R1 = Rotary Potentiometer (Small) [maximum_resistance=100kΩ package=THT]
  LED2 = LED - 5mm [color="Green (565nm)" package="5 mm [THT]"]
  LED3 = LED - 5mm [color="Yellow (595nm)" package="5 mm [THT]"]
  LED4 = LED - 5mm [color="Blue (470nm)" package="5 mm [THT]"]
  LED5 = LED - 5mm [color="Orange (620nm)" package="5 mm [THT]"]
  R2 = Resistor [tolerance=±5% resistance=470 package=THT]
  R3 = Resistor [tolerance=±5% resistance=470 package=THT]
  R4 = Resistor [tolerance=±5% resistance=470 package=THT]
  R5 = Resistor [tolerance=±5% resistance=470 package=THT]
  R6 = Resistor [tolerance=±5% resistance=470 package=THT]

nets:
  N1: Part1.A0, R1.wiper
  N2: Part1.D2, R2.Pin_0
  N3: Part1.D3_PWM, R3.Pin_0
  N4: Part1.D4, R4.Pin_0
  N5: Part1.D5_PWM, R5.Pin_0
  N6: Part1.D6_PWM, R6.Pin_0
  N7: Part1.5V, R1.leg2
  N8: Part1.GND, LED1.cathode, R1.leg1, LED2.cathode, LED3.cathode, LED4.cathode, LED5.cathode
  N9: LED1.anode, R2.Pin_1
  N10: LED2.anode, R3.Pin_1
  N11: LED3.anode, R4.Pin_1
  N12: LED4.anode, R5.Pin_1
  N13: LED5.anode, R6.Pin_1
