# Fritzing sketch miercoles4 (saved by Fritzing 0.9.1b)
breadboards: 1

parts:
  U1 = MIC [package=mic_electret_smd]
  Part1 = Arduino Uno (Rev3)
  R1 = Resistor [tolerance=±5% resistance=220 package=THT]
  R2 = Rotary Potentiometer (Small) [maximum_resistance=100kΩ package=THT]

nets:
  N1: U1.1, Part1.GND, R2.leg1
  N2: U1.2, Part1.A5/SCL, R1.Pin_1
  N3: Part1.A0, R2.wiper
  N4: Part1.5V, R1.Pin_0, R2.leg2
